# Fritzing sketch Schematics (saved by Fritzing 0.9.3b)
breadboards: 1

parts:
  Part1 = Arduino Nano (Rev3.0)
  RHT1 = Humidity and Temperature Sensor RHT03
  R1 = Resistor [tolerance=±5% resistance=220 package=THT]
  Part2 = NRF24L01+ Breakout Board
  Part3 = Arduino Uno (Rev3)
  Part4 = NRF24L01+ Breakout Board
  LCD1 = LCD screen
  LCM1602_IIC2 = LCM1602 IIC [part_number="LCM1602 IIC" chip_label="LCM1602 IIC" package="DIP (Dual Inline) [THT]"]
  Part5 = PowerBoost 500 Charger
  BAT1 = Battery Holders [package=lipo-1100mAh]

nets:
  GND: Part1.GND, RHT1.GND_2, Part2.GND, Part5.GND
  N1: Part1.D7, Part2.CS
  N2: Part1.D8, Part2.CE
  N3: Part1.D10, Part2.MISO
  N4: Part1.D11/MOSI, Part2.MOSI
  N5: Part1.D12/MISO, Part2.SCK
  5V: Part1.5V, RHT1.Vcc, R1.Pin_0, Part5.5.0V
  N6: Part1.A0, RHT1.Data-signal, R1.Pin_1
  3V3: Part1.3V3, Part2.VCC
  N7: Part3.A4/SDA, LCM1602_IIC2.SDA
  N8: Part3.A5/SCL, LCM1602_IIC2.SCL
  N9: Part3.D8, Part4.CE
  N10: Part3.D10_PWM/SS, Part4.MISO
  N11: Part3.D11_PWM/MOSI, Part4.MOSI
  N12: Part3.D12/MISO, Part4.SCK
  N13: Part3.D7, Part4.CS
  3V3_2: Part3.3V3, Part4.VCC
  5V_2: Part3.5V, LCM1602_IIC2.VCC
  GND_2: Part3.GND, Part4.GND, LCM1602_IIC2.GND
  VSS: LCD1.VSS, LCM1602_IIC2.VSS
  VDD: LCD1.VDD, LCM1602_IIC2.VDD
  N14: LCD1.V0, LCM1602_IIC2.V0
  N15: LCD1.RS, LCM1602_IIC2.RS
  N16: LCD1.R/W, LCM1602_IIC2.RW
  N17: LCD1.E, LCM1602_IIC2.E
  N18: LCD1.DB0, LCM1602_IIC2.D0
  N19: LCD1.DB1, LCM1602_IIC2.D1
  N20: LCD1.DB2, LCM1602_IIC2.D2
  N21: LCD1.DB3, LCM1602_IIC2.D3
  N22: LCD1.DB4, LCM1602_IIC2.D4
  N23: LCD1.DB5, LCM1602_IIC2.D5
  N24: LCD1.DB6, LCM1602_IIC2.D6
  N25: LCD1.DB7, LCM1602_IIC2.D7
  N26: LCD1.LED+, LCM1602_IIC2.A
  N27: LCD1.LED-, LCM1602_IIC2.K
  N28: Part5.GND_BAT_IN, BAT1.-
  N29: Part5.VBAT_IN, BAT1.+

custom parts:
  LCM1602 IIC: I2C-Module to use a 1602 or 2004 LCD on with the wire.h libory Serial LCD Modul
